// Logisim project project circuit ddca.circ as structural Verilog: 1 circuit, main circuit main
module main (
  input  A,
  input  B,
  input  C,
  input  D,
  input  A_prime,
  input  B_prime,
  input  C_prime,
  input  D_prime,
  output P,
  output out_10
);

  wire xor_1_out, xor_2_out, xor_3_out, xor_4_out, xor_6_out;

  xor xor_1 (xor_1_out, A, B);
  xor xor_2 (xor_2_out, C, D);
  xor xor_3 (xor_3_out, A_prime, B_prime);
  xor xor_4 (xor_4_out, C_prime, D_prime);
  xor xor_5 (P, xor_1_out, xor_2_out);
  xor xor_6 (xor_6_out, xor_3_out, xor_4_out);
  not not_1 (out_10, xor_6_out);

  // Notes on the sheet:
  //   Transmitter(Parity Generator)
  //   A (+) B
  //   C(+) D
  //   A' (+) B'
  //   C' (+) D"
  //   S
  //   Receiver (Parity Checker) 
  //   Error = s
  //   Error Detection Output
endmodule
